# Fritzing sketch circuit (saved by Fritzing 0.9.3b)
breadboards: 1

parts:
  Part1 = Arduino Mega 2560 (Rev3)
  Part3 = Analog Digital MUX Breakout
  Part4 = Analog Digital MUX Breakout
  U2 = Battery Holders [package=battery-aa-kit]
  U3 = Battery Holders [package=battery-aa-kit]
  U6 = Battery Holders [package=battery-aa-kit]
  DS1 = DS18B20 1-Wire Temperature Sensor [part_number=DS18B20]
  R1 = Resistor [tolerance=±5% resistance=4.7k package="0603 [SMD]"]
  R2 = Resistor [tolerance=±5% resistance=100k package="0603 [SMD]"]
  R3 = Resistor [tolerance=±5% resistance=1k package="0603 [SMD]"]

nets:
  N1: Part1.A0, Part3.SIG
  VCC: Part1.5V, Part3.VCC, Part4.VCC, DS1.VDD, R1.Pin_0
  GND: Part1.GND, Part3.GND, Part3.EN, Part4.C13, Part4.GND, Part4.EN, Part4.SIG, U3.-, DS1.GND, R3.Pin_0
  N2: Part1.D49, R2.Pin_0, R3.Pin_1
  N3: Part1.D53, DS1.DQ, R1.Pin_1
  N4: Part3.C13, Part4.C14, U2.-, U3.+
  N5: Part3.C14, Part4.C15, U2.+, U6.-
  N6: Part3.C15, U6.+, R2.Pin_1
  N7: Part3.S0, Part4.S0
  N8: Part3.S1, Part4.S1
  N9: Part3.S2, Part4.S2
  N10: Part3.S3, Part4.S3
